# Fritzing sketch Wiring (saved by Fritzing 1.0.0rc)

parts:
  J1 = male pin header, 4 pins [form="♂ (male)"]
  J2 = female pin header, 4 pins [form="♀ (female)"]
  J3 = female pin header, 1 pin [form="♀ (female)"]
  J4 = female pin header, 1 pin [form="♀ (female)"]
  J5 = female pin header, 2 pins [form="♀ (female)"]
  J6 = female pin header, 2 pins [form="♀ (female)"]
  part = Raspberry Pi 3 [part_number=Sender]
  part_2 = Raspberry Pi 4B [part_number=Receiver]

nets:
  N1: J1.pin1, part_2.5V
  N2: J1.pin3, part_2.GPIO2
  GND: J1.pin4, part.GND, part_2.GND
  N3: J2.pin1, J5.pin1
  N4: J2.pin2, J5.pin2
  N5: J2.pin3, J6.pin1
  N6: J2.pin4, J3.pin1
  N7: J4.pin1, J6.pin2
  N8: part.GPIO15, part_2.GPIO14
  N9: part.GPIO14, part_2.GPIO15

notes:
  USB Cable
